// Digital circuit 02.dig as structural Verilog
module _02 (
  input  [15:0] A,
  input  \input ,
  input  clk,
  input  [3:0] R,
  output [15:0] nroot,
  output busy,
  output [31:0] Prod,
  output [31:0] out_8,
  output [31:0] out_9,
  output [31:0] out_10,
  output [15:0] out_11
);

  wire comparator_2_eq, comparator_2_gt, multiplexer_7_out, or_1_out, or_2_out, R_1;
  wire [15:0] add_1_s, multiplexer_1_out, multiplexer_2_out, sub_1_s;
  wire [31:0] multiplexer_3_out, multiplexer_4_out, multiplexer_5_out, multiplexer_6_out;
  wire [63:0] mul_1_mul, mul_2_mul;
  wire [63:32] mul_3_mul, X_2_mul, X_4_mul, X_8_mul;

  Comparator #(.Bits(4)) comparator_1 (.a(R), .b(4'b0001), .eq(R_1));  // open: gt, lt
  Add #(.Bits(16)) add_1 (.a(out_11), .b(16'h1), .c_i(1'b0), .s(add_1_s));  // open: c_o
  Mul #(.Bits(32)) X_2 (.a({{16{1'b0}}, out_11}), .b({{16{1'b0}}, out_11}), .mul({X_2_mul, out_8}));
  Mul #(.Bits(32)) X_4 (.a(out_8), .b(out_8), .mul({X_4_mul, out_9}));
  Mul #(.Bits(32)) X_8 (.a(out_9), .b(out_9), .mul({X_8_mul, out_10}));
  Comparator #(.Bits(32)) comparator_2 (
    .a({{16{1'b0}}, A}), .b(Prod), .gt(comparator_2_gt), .eq(comparator_2_eq));  // open: lt
  Multiplexer #(.Bits(16)) multiplexer_1 (.sel(busy), .in_0(out_11), .in_1(add_1_s), .out(multiplexer_1_out));
  Multiplexer #(.Bits(16)) multiplexer_2 (
    .sel(\input ), .in_0(multiplexer_1_out), .in_1(16'h2), .out(multiplexer_2_out));
  or or_1 (or_1_out, comparator_2_gt, comparator_2_eq);
  Multiplexer #(.Bits(32)) multiplexer_3 (
    .sel(R[0]), .in_0(32'h1), .in_1({{16{1'b0}}, out_11}), .out(multiplexer_3_out));
  Multiplexer #(.Bits(32)) multiplexer_4 (.sel(R[1]), .in_0(32'h1), .in_1(out_8), .out(multiplexer_4_out));
  Multiplexer #(.Bits(32)) multiplexer_5 (.sel(R[2]), .in_0(32'h1), .in_1(out_9), .out(multiplexer_5_out));
  Multiplexer #(.Bits(32)) multiplexer_6 (.sel(R[3]), .in_0(32'h1), .in_1(out_10), .out(multiplexer_6_out));
  Multiplexer multiplexer_7 (.sel(R_1), .in_0(or_1_out), .in_1(1'b0), .out(multiplexer_7_out));
  or or_2 (or_2_out, busy, \input );
  Mul #(.Bits(32)) mul_1 (.a(multiplexer_3_out), .b(multiplexer_4_out), .mul(mul_1_mul));
  Mul #(.Bits(32)) mul_2 (.a(multiplexer_5_out), .b(multiplexer_6_out), .mul(mul_2_mul));
  Multiplexer multiplexer_8 (.sel(\input ), .in_0(multiplexer_7_out), .in_1(1'b1), .out(busy));
  Register #(.Bits(16)) X (.D(multiplexer_2_out), .C(clk), .en(or_2_out), .Q(out_11));
  Mul #(.Bits(32)) mul_3 (.a(mul_1_mul[31:0]), .b(mul_2_mul[31:0]), .mul({mul_3_mul, Prod}));
  Sub #(.Bits(16)) sub_1 (.a(out_11), .b(16'h1), .c_i(1'b0), .s(sub_1_s));  // open: c_o
  Multiplexer #(.Bits(16)) multiplexer_9 (.sel(R_1), .in_0(sub_1_s), .in_1(A), .out(nroot));

  // Other names for the same wires on the sheet: res[31:0] = Prod; x[15:0] = out_11

  // Notes on the sheet:
  //   clk: Hz: 5
endmodule

/* Test case TestCase1:
clk A R input nroot busy
0 0 0 0 X 0
1 0 0 0 X 0
0 0 0 0 X 0
1 0 0 0 X 0
0 2 2 1 X X
1 2 2 1 X X
repeat (255) C 2 2 0 X X
0 2 2 0 1 0
1 2 2 0 1 0
0 0 0 0 X 0
1 0 0 0 X 0
0 0 0 0 X 0
1 0 0 0 X 0
0 4 2 1 X X
1 4 2 1 X X
repeat (255) C 4 2 0 X X
0 4 2 0 2 0
1 4 2 0 2 0
0 0 0 0 X 0
1 0 0 0 X 0
0 0 0 0 X 0
1 0 0 0 X 0
0 8 2 1 X X
1 8 2 1 X X
repeat (255) C 8 2 0 X X
0 8 2 0 2 0
1 8 2 0 2 0
0 0 0 0 X 0
1 0 0 0 X 0
0 0 0 0 X 0
1 0 0 0 X 0
0 16 2 1 X X
1 16 2 1 X X
repeat (255) C 16 2 0 X X
0 16 2 0 4 0
1 16 2 0 4 0
*/

/* Test case TestCase4:
clk A R input nroot busy
0 0 0 0 X 0
1 0 0 0 X 0
0 0 0 0 X 0
1 0 0 0 X 0
0 65530 12 1 X X
1 65530 12 1 X X
repeat (255) C 65530 12 0 X X
0 65530 12 0 2 0
1 65530 12 0 2 0
0 0 0 0 X 0
1 0 0 0 X 0
0 0 0 0 X 0
1 0 0 0 X 0
0 60000 3 1 X X
1 60000 3 1 X X
repeat (255) C 60000 3 0 X X
0 60000 3 0 39 0
1 60000 3 0 39 0
0 0 0 0 X 0
1 0 0 0 X 0
0 0 0 0 X 0
1 0 0 0 X 0
0 55124 4 1 X X
1 55124 4 1 X X
repeat (255) C 55124 4 0 X X
0 55124 4 0 15 0
1 55124 4 0 15 0
0 0 0 0 X 0
1 0 0 0 X 0
0 0 0 0 X 0
1 0 0 0 X 0
0 14778 5 1 X X
1 14778 5 1 X X
repeat (255) C 14778 5 0 X X
0 14778 5 0 6 0
1 14778 5 0 6 0
*/

/* Test case TestCase8:
clk A R input nroot busy
0 0 0 0 X 0
1 0 0 0 X 0
0 0 0 0 X 0
1 0 0 0 X 0
0 65535 1 1 X X
1 65535 1 1 X X
repeat (255) C 65535 1 0 X X
0 65535 1 0 65535 0
1 65535 1 0 65535 0
0 0 0 0 X 0
1 0 0 0 X 0
0 0 0 0 X 0
1 0 0 0 X 0
0 64000 15 1 X X
1 64000 15 1 X X
repeat (255) C 64000 15 0 X X
0 64000 15 0 2 0
1 64000 15 0 2 0
0 0 0 0 X 0
1 0 0 0 X 0
0 0 0 0 X 0
1 0 0 0 X 0
0 12000 5 1 X X
1 12000 5 1 X X
repeat (255) C 12000 5 0 X X
0 12000 5 0 6 0
1 12000 5 0 6 0
0 0 0 0 X 0
1 0 0 0 X 0
0 0 0 0 X 0
1 0 0 0 X 0
0 65535 15 1 X X
1 65535 15 1 X X
repeat (255) C 65535 15 0 X X
0 65535 15 0 2 0
1 65535 15 0 2 0
*/
